# Fritzing sketch ESP8266-Arduino (saved by Fritzing 0.9.2b)
breadboards: 1

parts:
  Bauteil1 = Arduino Uno (Rev3)
  R1 = Resistor [tolerance=±5% resistance=1k package=THT]
  R2 = Resistor [tolerance=±5% resistance=680 package=THT]
  U1 = ESP8266 WiFi Module [part_number=ESP8266]
  R5 = Resistor [tolerance=±5% resistance=3.3k package="0603 [SMD]"]
  R6 = Resistor [tolerance=±5% resistance=3.3k package="0603 [SMD]"]
  R7 = Resistor [tolerance=±5% resistance=3.3k package="0603 [SMD]"]
  R8 = Resistor [tolerance=±5% resistance=3.3k package="0603 [SMD]"]
  S1 = Round Pushbutton

nets:
  GND: Bauteil1.GND, R1.Pin_0, U1.GND, S1.leg1
  N1: Bauteil1.D0/RX, U1.TXD
  N2: Bauteil1.D1/TX, R2.Pin_1
  N3: R1.Pin_1, R2.Pin_0
  N4: U1.VCC, R5.Pin_1, R6.Pin_0, R7.Pin_0, R8.Pin_0
  N5: U1.GPIO_0, R6.Pin_1, S1.leg0
  N6: U1.RST, R5.Pin_0
  N7: U1.GPIO_2, R7.Pin_1
  N8: U1.CH_PD, R8.Pin_1

notes:
  GND
  RxD
  TxD
  + 3.3 V
  VCC
  RST
  CH_PD
  GPIO_0
  GPIO_2
  R3 - R6: 3.3k each
  ESP8266-01
  Programming Switch (optional)

custom parts:
  ESP8266 WiFi Module: Generic WiFi Module based on the ESP8266 with onboard PCB antenna and UART communications
