# Fritzing sketch HC-05-Arduino (saved by Fritzing 0.9.2b)
breadboards: 1

parts:
  Bauteil1 = Arduino Uno (Rev3)
  R1 = Resistor [tolerance=±5% resistance=1k package=THT]
  R2 = Resistor [tolerance=±5% resistance=680 package=THT]
  U2 = HC-05 Bluetooth Transceiver Breakout Board, 5V, 6pin [chip_label=IC package=SIP]

nets:
  N1: Bauteil1.D8, U2.TX
  N2: Bauteil1.D9_PWM, R2.Pin_1
  GND: Bauteil1.GND, R1.Pin_0, U2.GND
  5V: Bauteil1.5V, U2.VCC
  N3: R1.Pin_1, R2.Pin_0, U2.RX

notes:
  GND
  RxD
  TxD
  +5V
  HC-05 Bluetooth Module

custom parts:
  HC-05 Bluetooth Transceiver Breakout Board, 5V, 6pin: Breakout board for HC-05 with 5V-to-3V translation, command mode pin (KEY) and STATE pin. http://www.ebay.com/itm/HC-05-Bluetooth-Transceiver-Host-Slave-Master-Module-Wireless-Serial-6pin-/221158958927?pt=LH_DefaultDomain_0&hash=item337e19e74f
