# Fritzing sketch Raspberry-I2C-Arduino (saved by Fritzing 0.9.2b)

parts:
  Bauteil1 = Arduino Uno (Rev3)
  Raspberry_Pi1 = Raspberry Pi 2

nets:
  GND: Bauteil1.GND, Raspberry_Pi1.GND
  N1: Bauteil1.A4/SDA, Raspberry_Pi1.GPIO2
  N2: Bauteil1.A5/SCL, Raspberry_Pi1.GPIO3

notes:
  USB cable
  SDA
  SCL
  GND
