# Fritzing sketch Raspberry-Software-I2C-Arduino (saved by Fritzing 0.9.2b)

parts:
  Bauteil1 = Arduino Uno (Rev3)
  Raspberry_Pi1 = Raspberry Pi 2

nets:
  N1: Bauteil1.A0, Raspberry_Pi1.GPIO3
  N2: Bauteil1.A1, Raspberry_Pi1.GPIO2
  GND: Bauteil1.GND, Raspberry_Pi1.GND

notes:
  USB cable
  SDA
  SCL
  GND
