# Fritzing sketch Raspberry-UART-Arduino (saved by Fritzing 0.9.2b)
breadboards: 1

parts:
  Bauteil1 = Arduino Uno (Rev3)
  Raspberry_Pi1 = Raspberry Pi 2
  R1 = Resistor [tolerance=±5% resistance=1k package=THT]
  R2 = Resistor [tolerance=±5% resistance=680 package=THT]

nets:
  GND: Bauteil1.GND, Raspberry_Pi1.GND, R1.Pin_0
  N1: Bauteil1.D0/RX, Raspberry_Pi1.GPIO14
  N2: Bauteil1.D1/TX, R2.Pin_1
  N3: Raspberry_Pi1.GPIO15, R1.Pin_1, R2.Pin_0

notes:
  USB cable
  GND
  RxD
  TxD
